# Fritzing sketch Scheme (saved by Fritzing 0.8.7b)
perfboards: 1

parts:
  Onderdeel1 = Arduino Uno (Rev3)
  Q1 = Basic FET N-Channel [package="TO220 [THT]"]
  Q2 = Basic FET N-Channel [package="TO220 [THT]"]
  Q3 = Basic FET N-Channel [package="TO220 [THT]"]
  FC-1 = Sound Sensor
  Power_plug1 = Power plug
  S1 = Round Pushbutton
  S2 = Toggle Switch [package=THT]
  RGB_Strip_LED2 = RGB Strip LED
  R1 = Resistor [tolerance=±5% resistance=330 package=THT]

nets:
  N1: Onderdeel1.D11_PWM/MOSI, FC-1.OUT
  GND: Onderdeel1.GND, Q1.source, Q3.source, FC-1.GND, Power_plug1.GND, R1.Pin_1
  N2: Onderdeel1.D3_PWM, Q1.gate
  N3: Onderdeel1.D4, R1.Pin_0
  N4: Onderdeel1.D5_PWM, Q2.gate
  N5: Onderdeel1.D6_PWM, Q3.gate
  5V: Onderdeel1.5V, FC-1.VCC, S1.leg1
  N6: Onderdeel1.VIN, S2.COM, RGB_Strip_LED2.Common_Connect#4
  N7: Q1.drain, RGB_Strip_LED2.Red_Connect#6
  N8: Q2.drain, RGB_Strip_LED2.Green_Connect#7
  N9: Q3.drain, RGB_Strip_LED2.Blue_Connect#5
  N10: Power_plug1.VCC, S2.L1

custom parts:
  RGB Strip LED: A tri-color Strip LED with red, green and blue. Pin order: red - common cathode - blue - green
